// Logisim project adder_subtractor.circ as structural Verilog: 4 circuits, main circuit main
module main (
  input  in_1,
  input  in_2,
  input  in_3,
  output out_4,
  output out_5
);

  wire and_1_out, and_2_out, xor_1_out;

  xor xor_1 (xor_1_out, in_2, in_3);
  and and_1 (and_1_out, in_2, in_3);
  xor xor_2 (out_4, in_1, xor_1_out);
  and and_2 (and_2_out, in_1, xor_1_out);
  or or_1 (out_5, and_2_out, and_1_out);
endmodule

module fa (
  input  [3:0] in_1,
  input  [3:0] in_2,
  output [3:0] out_3,
  output out_4
);

  wire main_1_out_5, main_2_out_5, main_3_out_5;

  main main_1 (.in_1(1'b0), .in_2(in_1[0]), .in_3(in_2[0]), .out_4(out_3[0]), .out_5(main_1_out_5));
  main main_2 (.in_1(main_1_out_5), .in_2(in_1[1]), .in_3(in_2[1]), .out_4(out_3[1]), .out_5(main_2_out_5));
  main main_3 (.in_1(main_2_out_5), .in_2(in_1[2]), .in_3(in_2[2]), .out_4(out_3[2]), .out_5(main_3_out_5));
  main main_4 (.in_1(main_3_out_5), .in_2(in_1[3]), .in_3(in_2[3]), .out_4(out_3[3]), .out_5(out_4));
endmodule

module _4fa (
  input  [3:0] in_1,
  input  [3:0] in_2,
  input  [3:0] in_3,
  input  [3:0] in_4,
  output [3:0] out_5,
  output out_6,
  output [3:0] out_7,
  output [3:0] out_8
);

  wire [3:0] not_1_out;

  fa fa_1 (.in_1(in_1), .in_2(in_2), .out_3(out_5), .out_4(out_6));
  not not_1 (not_1_out[0], in_4[0]);
  not not_2 (not_1_out[1], in_4[1]);
  not not_3 (not_1_out[2], in_4[2]);
  not not_4 (not_1_out[3], in_4[3]);
  fa fa_2 (.in_1(in_3), .out_3(out_7));  // open: in_2, out_4
  fa fa_3 (.in_2(4'b0001), .out_3(out_8));  // open: in_1, out_4
endmodule

module subtractor (
  input  [3:0] _4_Bit_Binary_A,
  input  [3:0] _4_Bit_Binary_B,
  output out_3,
  output out_4,
  output out_5,
  output out_6,
  output out_7
);

  wire main_2_out_5, main_3_out_5, main_4_out_5, xor_1_out, xor_2_out, xor_3_out, xor_4_out;

  xor xor_1 (xor_1_out, _4_Bit_Binary_B[3], 1'b1);
  main main_1 (.in_1(main_2_out_5), .in_2(xor_1_out), .in_3(_4_Bit_Binary_A[3]), .out_4(out_4), .out_5(out_3));
  main main_2 (.in_1(main_3_out_5), .in_2(xor_2_out), .in_3(_4_Bit_Binary_A[2]), .out_4(out_5), .out_5(main_2_out_5));
  xor xor_2 (xor_2_out, _4_Bit_Binary_B[2], 1'b1);
  main main_3 (.in_1(main_4_out_5), .in_2(xor_3_out), .in_3(_4_Bit_Binary_A[1]), .out_4(out_6), .out_5(main_3_out_5));
  xor xor_3 (xor_3_out, _4_Bit_Binary_B[1], 1'b1);
  xor xor_4 (xor_4_out, _4_Bit_Binary_B[0], 1'b1);
  main main_4 (.in_1(1'b1), .in_2(xor_4_out), .in_3(_4_Bit_Binary_A[0]), .out_4(out_7), .out_5(main_4_out_5));
endmodule
