// Logisim project fulladder.circ as structural Verilog: 2 circuits, main circuit main
module main (
  input  Carry_In,
  input  A,
  input  B,
  output Sum,
  output Carry_Out
);

  wire and_1_out, and_2_out, xor_1_out;

  xor xor_1 (xor_1_out, A, B);
  and and_1 (and_1_out, A, B);
  xor xor_2 (Sum, Carry_In, xor_1_out);
  and and_2 (and_2_out, Carry_In, xor_1_out);
  or or_1 (Carry_Out, and_2_out, and_1_out);
endmodule

module Full_Adder (
  input  [3:0] in_1,
  input  [3:0] in_2,
  output [3:0] out_3,
  output Carry_Out
);

  wire main_1_carry_out, main_2_carry_out, main_3_carry_out;

  main main_1 (.Carry_In(1'b0), .A(in_1[0]), .B(in_2[0]), .Sum(out_3[0]), .Carry_Out(main_1_carry_out));
  main main_2 (.Carry_In(main_1_carry_out), .A(in_1[1]), .B(in_2[1]), .Sum(out_3[1]), .Carry_Out(main_2_carry_out));
  main main_3 (.Carry_In(main_2_carry_out), .A(in_1[2]), .B(in_2[2]), .Sum(out_3[2]), .Carry_Out(main_3_carry_out));
  main main_4 (.Carry_In(main_3_carry_out), .A(in_1[3]), .B(in_2[3]), .Sum(out_3[3]), .Carry_Out(Carry_Out));
endmodule
